// Logisim project control unit.circ as structural Verilog: 1 circuit, main circuit main
module main (
  input  [15:0] IR,
  input  in_2,
  input  in_3,
  input  in_4,
  output LOAD_PC,
  output INCPC,
  output LOAD_AR,
  output INCAR,
  output LOAD_DR,
  output INCDR,
  output LOAD_AC,
  output INCAC,
  output LOAD_IR,
  output LOAD_M_AR
);

  wire and_1_out, and_2_out, and_3_out, and_4_out, and_5_out, and_6_out, and_7_out, and_8_out, and_9_out,
       and_10_out, and_11_out, and_12_out, and_13_out, and_14_out, and_15_out, and_16_out, and_17_out,
       and_18_out, and_19_out, and_20_out, and_23_out, B1, B2, B6, D1, D2, D3, D4, D5, D6, D7, DO, not_1_out,
       not_2_out, not_3_out, not_4_out, not_5_out, not_6_out, not_7_out, not_8_out, T2, T3, T4, T5, T6, T7,
       TO;
  wire [3:0] main_1_p4;

  Decoder #(.select(3)) decoder_1 (
    .out0(DO), .out1(D1), .out2(D2), .out3(D3), .out4(D4), .out5(D5), .out6(D6), .out7(D7), .sel(IR[14:12]));  // open: en
  not not_1 (not_1_out, IR[15]);
  not not_2 (not_2_out, IR[15]);
  not not_3 (not_3_out, IR[15]);
  not not_4 (not_4_out, IR[15]);
  // sequencial_counter_main main_1: pin names not known; wires that end beside it: in_2, in_3, in_4, main_1_p4
  and and_1 (and_1_out, T5, D1);
  and and_2 (and_2_out, D2, T5);
  and and_3 (and_3_out, D7, T3, not_2_out, IR[9]);
  and and_4 (and_4_out, D7, not_3_out, T3, B6);
  Decoder #(.select(4)) decoder_2 (
    .out0(TO), .out1(LOAD_IR), .out2(T2), .out3(T3), .out4(T4), .out5(T5), .out6(T6), .out7(T7),
    .sel(main_1_p4));  // open: out8, out9, out10, out11, out12, out13, out14, out15, en
  and and_5 (and_5_out, T5, DO);
  and and_6 (and_6_out, not_1_out, T3, D7, IR[11]);
  and and_7 (and_7_out, D7, not_4_out, T3, IR[7]);
  and and_8 (and_8_out, D5, T4);
  not not_5 (not_5_out, IR[15]);
  and and_9 (and_9_out, B2, D7, IR[15], T3);
  not not_6 (not_6_out, IR[15]);
  and and_10 (and_10_out, D6, T6);
  and and_11 (and_11_out, D3, T4);
  and and_12 (and_12_out, not_5_out, D7, B1, T3);
  not not_7 (not_7_out, IR[15]);
  or or_1 (LOAD_AC, and_5_out, and_1_out, and_2_out, and_6_out, and_3_out, and_4_out, and_7_out);
  or or_2 (LOAD_M_AR, and_10_out, and_11_out, and_8_out);
  and and_13 (and_13_out, D4, T4);
  and and_14 (and_14_out, D5, T5);
  and and_15 (and_15_out, D6, T6);
  and and_16 (and_16_out, D7, not_6_out, T3, IR[4]);
  and and_17 (and_17_out, not_7_out, D7, T3);
  and and_18 (and_18_out, DO, T4);
  and and_19 (and_19_out, D1, T4);
  and and_20 (and_20_out, D2, T4);
  or or_3 (LOAD_PC, and_13_out, and_14_out);
  and and_21 (INCAR, D5, T4);
  and and_22 (INCDR, D6, T5);
  or or_4 (INCPC, and_15_out, and_12_out, LOAD_IR, and_9_out, and_16_out, IR[3]);
  or or_5 (LOAD_AR, TO, T2, and_17_out);
  and and_23 (and_23_out, T4, D6);
  not not_8 (not_8_out, IR[15]);
  or or_6 (LOAD_DR, and_18_out, and_19_out, and_20_out, and_23_out);
  and and_24 (INCAC, D7, not_8_out, T3, IR[5]);

  // Other names for the same wires on the sheet: B3 = IR[3]; B4 = IR[4]; B5 = IR[5]; B7 = IR[7]; B9 = IR[9];
  //   B11 = IR[11]; I = IR[15]; T1 = LOAD_IR
endmodule
