// Logisim project project.circ as structural Verilog: 2 circuits, main circuit main
module main (
  input  in_1,
  input  in_2,
  input  in_3,
  input  in_4,
  input  [2:0] in_5,
  input  in_6,
  input  in_7,
  input  in_8,
  input  in_9,
  input  in_10,
  input  in_11,
  input  in_12
);

  wire ALU_eout, clock_1_out, d_ff_1_q, INC_AC, INC_AR, INC_DR, INC_PC, LOAD_AC, LOAD_AR, LOAD_DR, LOAD_IR,
       LOAD_M_AR, LOAD_PC;
  wire [7:0] bit_extender_1_out, INPR_q;
  wire [11:0] AR_q, bit_extender_2_out, bit_extender_3_out, PC_q;
  wire [15:0] AC_q, ALU_ac_2, bit_extender_4_out, bit_extender_5_out, DR_q, IR, IR_q, multiplexer_1_out,
       ram_1_data;

  Clock clock_1 (.out(clock_1_out));
  Bit_Extender #(.in_width(16), .out_width(8)) bit_extender_1 (.in(multiplexer_1_out), .out(bit_extender_1_out));
  ALU ALU (
    .AC(AC_q), .DR(DR_q), .INPR(INPR_q), .Ein(d_ff_1_q), .in_1(in_8), .in_2(in_7), .in_3(in_6), .in_4(in_4),
    .in_5(in_3), .in_6(in_2), .in_7(in_1), .Eout(ALU_eout), .AC_2(ALU_ac_2));
  Bit_Extender #(.in_width(16), .out_width(12)) bit_extender_2 (.in(multiplexer_1_out), .out(bit_extender_2_out));
  Bit_Extender #(.in_width(16), .out_width(12)) bit_extender_3 (.in(multiplexer_1_out), .out(bit_extender_3_out));
  D_Flip_Flop d_ff_1 (.clk(clock_1_out), .D(ALU_eout), .Q(d_ff_1_q));  // open: Qn, preset, en, reset
  Counter #(.width(12), .max('hfff)) AR (
    .load(LOAD_AR), .D(bit_extender_2_out), .count(INC_AR), .Q(AR_q), .clk(clock_1_out));  // open: carry, clr
  Counter #(.width(12), .max('hfff)) PC (
    .load(LOAD_PC), .D(bit_extender_3_out), .count(INC_PC), .Q(PC_q), .clk(clock_1_out));  // open: carry, clr
  Counter #(.width(16), .max('hffff)) DR (
    .load(LOAD_DR), .D(multiplexer_1_out), .count(INC_DR), .Q(DR_q), .clk(clock_1_out));  // open: carry, clr
  Counter #(.width(16), .max('hffff)) AC (
    .load(LOAD_AC), .D(ALU_ac_2), .count(INC_AC), .Q(AC_q), .clk(clock_1_out));  // open: carry, clr
  Register INPR (.en(in_10), .Q(INPR_q), .clk(clock_1_out));  // open: D, clr
  Counter #(.width(16), .max('hffff)) u_IR (
    .load(LOAD_IR), .D(multiplexer_1_out), .count(in_11), .Q(IR_q), .clk(clock_1_out));  // open: carry, clr
  Counter OUTR (.load(in_9), .D(bit_extender_1_out), .count(in_12), .clk(clock_1_out));  // open: Q, carry, clr
  RAM #(.addrWidth(12), .dataWidth(16), .bus("separate")) ram_1 (
    .addr(AR_q), .din(multiplexer_1_out), .data(ram_1_data), .ld(LOAD_M_AR));  // open: str, sel, clk, clr
  assign bit_extender_4_out = {{4{1'b0}}, AR_q};  // Bit_Extender bit_extender_4
  assign bit_extender_5_out = {{4{1'b0}}, PC_q};  // Bit_Extender bit_extender_5
  Multiplexer #(.select(3), .width(16), .enable("false")) multiplexer_1 (
    .in1(bit_extender_4_out), .in2(bit_extender_5_out), .in3(DR_q), .in4(AC_q), .in5(IR_q), .in7(ram_1_data),
    .out(multiplexer_1_out), .sel(in_5));  // open: in0, in6
  // control_unit_main main_1: pin names not known; wires that end beside it: IR, LOAD_PC, INC_PC, LOAD_AR, INC_AR, LOAD_DR, INC_DR, LOAD_AC, INC_AC, LOAD_IR, LOAD_M_AR
endmodule

module ALU (
  input  in_1,
  input  in_2,
  input  in_3,
  input  in_4,
  input  in_5,
  input  in_6,
  input  in_7,
  input  [15:0] AC,
  input  [15:0] DR,
  input  [7:0] INPR,
  input  Ein,
  output [15:0] AC_2,
  output Eout
);

  wire adder_1_cout, not_2_out;
  wire [1:0] bit_extender_1_out, or_1_out;
  wire [2:0] priority_encoder_1_out;
  wire [15:0] adder_1_out, and_1_out, bit_extender_2_out, not_1_out;

  Priority_Encoder priority_encoder_1 (
    .in0(in_7), .in1(in_6), .in2(in_5), .in3(in_4), .in4(in_3), .in5(in_2), .in6(in_1),
    .out(priority_encoder_1_out));  // open: in7, en_in, gs, en_out
  assign and_1_out = AC & DR;  // AND_Gate and_1, 16 bits wide
  assign bit_extender_1_out = {{1{in_6}}, in_6};  // Bit_Extender bit_extender_1
  Adder #(.width(16)) adder_1 (.a(AC), .b(DR), .out(adder_1_out), .cout(adder_1_cout));  // open: cin
  assign bit_extender_2_out = {{8{1'b0}}, INPR};  // Bit_Extender bit_extender_2
  Multiplexer #(.select(3), .width(16), .enable("false")) multiplexer_1 (
    .in0(and_1_out), .in1(adder_1_out), .in2(DR), .in3(bit_extender_2_out), .in4(not_1_out),
    .in5({Ein, AC[15:1]}), .in6({AC[14:0], Ein}), .out(AC_2), .sel(priority_encoder_1_out));  // open: in7
  assign not_1_out = ~AC;  // NOT_Gate not_1, 16 bits wide
  assign or_1_out = bit_extender_1_out | {in_1, in_2};  // OR_Gate or_1, 2 bits wide
  Multiplexer #(.select(2), .disabled(0), .enable("false")) multiplexer_2 (
    .in0(not_2_out), .in1(AC[0]), .in2(AC[15]), .in3(adder_1_cout), .out(Eout), .sel(or_1_out));
  not not_2 (not_2_out, 1'b1);
endmodule
