// Logisim project sequencial counter.circ as structural Verilog: 1 circuit, main circuit main
module main (
  input  ld_signal,
  input  [3:0] \input ,
  input  inr_signal,
  input  clr_signal,
  output [3:0] output_data_lines_prime
);

  wire clock_1_out, d_ff_1_q;

  Clock clock_1 (.out(clock_1_out));
  Counter #(.width(4), .max('hf)) counter_1 (
    .load(ld_signal), .D(\input ), .count(inr_signal), .Q(output_data_lines_prime), .clk(clock_1_out),
    .clr(d_ff_1_q));  // open: carry
  D_Flip_Flop d_ff_1 (.clk(clock_1_out), .D(clr_signal), .Q(d_ff_1_q));  // open: Qn, preset, en, reset
endmodule
